# Fritzing sketch traffic_light (saved by Fritzing 0.9.10b)
breadboards: 1

parts:
  Bauteil1 = Arduino Uno (Rev3)
  R1 = Resistor [tolerance=±5% power=0.25 resistance=220 package=THT]
  R2 = Resistor [tolerance=±5% power=0.25 resistance=220 package=THT]
  R4 = Resistor [tolerance=±5% power=0.25 resistance=220 package=THT]
  R5 = Resistor [tolerance=±5% power=0.25 resistance=220 package=THT]
  R6 = Resistor [tolerance=±5% power=0.25 resistance=220 package=THT]
  R7 = Resistor [tolerance=±5% power=0.25 resistance=220 package=THT]
  LED1 = LED - 5mm [color="Red (633nm)" current=0.030 package="5 mm [THT]"]
  LED2 = LED - 5mm [color="Red (633nm)" current=0.030 package="5 mm [THT]"]
  LED3 = LED - 5mm [color="Yellow (595nm)" current=0.030 package="5 mm [THT]"]
  LED4 = LED - 5mm [color="Yellow (595nm)" current=0.030 package="5 mm [THT]"]
  LED5 = LED - 5mm [color="Green (565nm)" current=0.030 package="5 mm [THT]"]
  LED6 = LED - 5mm [color="Green (565nm)" current=0.030 package="5 mm [THT]"]

nets:
  N1: Bauteil1.D9_PWM, LED5.anode
  N2: Bauteil1.D10_PWM/SS, LED4.anode
  N3: Bauteil1.D11_PWM/MOSI, LED1.anode
  N4: Bauteil1.D5_PWM, LED2.anode
  N5: Bauteil1.D6_PWM, LED3.anode
  N6: Bauteil1.D7, LED6.anode
  N7: Bauteil1.GND, R1.Pin_1, R2.Pin_1, R4.Pin_1, R5.Pin_1, R6.Pin_1, R7.Pin_1
  N8: R1.Pin_0, LED2.cathode
  N9: R2.Pin_0, LED5.cathode
  N10: R4.Pin_0, LED4.cathode
  N11: R5.Pin_0, LED1.cathode
  N12: R6.Pin_0, LED3.cathode
  N13: R7.Pin_0, LED6.cathode
